# Fritzing sketch PLC (saved by Fritzing 0.9.3b)
breadboards: 1

parts:
  U1 = Sharp PC817 [package=THT]
  U2 = Sharp PC817 [package=THT]
  U3 = Sharp PC817 [package=THT]
  U4 = Sharp PC817 [package=THT]
  LED1 = smd LED [color="Green (565nm)" package="1206 [SMD]"]
  R1 = Resistor [tolerance=±5% resistance=1k package=THT]
  LED2 = smd LED [color="Green (565nm)" package="1206 [SMD]"]
  R2 = Resistor [tolerance=±5% resistance=1k package=THT]
  LED3 = smd LED [color="Green (565nm)" package="1206 [SMD]"]
  R3 = Resistor [tolerance=±5% resistance=1k package=THT]
  LED4 = smd LED [color="Green (565nm)" package="1206 [SMD]"]
  R4 = Resistor [tolerance=±5% resistance=1k package=THT]
  J1 = Camdenboss CTB0158-2 [part_number=CTB0158-2 package=THT]
  J2 = Camdenboss CTB0158-2 [part_number=CTB0158-2 package=THT]
  J3 = Camdenboss CTB0158-2 [part_number=CTB0158-2 package=THT]
  J4 = Camdenboss CTB0158-2 [part_number=CTB0158-2 package=THT]
  R5 = Resistor [tolerance=±5% resistance=1k package=THT]
  R6 = Resistor [tolerance=±5% resistance=1k package=THT]
  R7 = Resistor [tolerance=±5% resistance=1k package=THT]  # not connected
  R8 = Resistor [tolerance=±5% resistance=1k package=THT]  # not connected
  Part1 = Arduino Uno (Rev3)

nets:
  N1: U1.Pin_1, LED1.cathode
  GND: U1.Pin_2, U1.Pin_3, U2.Pin_2, U2.Pin_3, U3.Pin_2, U3.Pin_3, U4.Pin_2, U4.Pin_3, J1.pin1, J2.pin1, J3.pin1, J4.pin1
  N2: U1.Pin_4, R5.Pin_0, Part1.D3_PWM
  N3: U2.Pin_1, LED2.cathode
  N4: U2.Pin_4, R6.Pin_0, Part1.D4
  N5: U3.Pin_1, LED3.cathode
  N6: U3.Pin_4, Part1.D7
  N7: U4.Pin_1, LED4.cathode
  N8: U4.Pin_4, Part1.D8
  N9: LED1.anode, R1.Pin_1
  N10: R1.Pin_0, J1.pin2
  N11: LED2.anode, R2.Pin_1
  N12: R2.Pin_0, J2.pin2
  N13: LED3.anode, R3.Pin_1
  N14: R3.Pin_0, J3.pin2
  N15: LED4.anode, R4.Pin_1
  N16: R4.Pin_0, J4.pin2
