# Fritzing sketch PLC2 (saved by Fritzing 0.9.3b)
breadboards: 1

parts:
  U1 = Sharp PC817 [package=THT]
  U2 = Sharp PC817 [package=THT]
  U3 = Sharp PC817 [package=THT]
  U4 = Sharp PC817 [package=THT]
  LED1 = smd LED [color="Green (565nm)" package="1206 [SMD]"]
  R1 = Resistor [tolerance=±5% resistance=1k package=THT]
  LED2 = smd LED [color="Green (565nm)" package="1206 [SMD]"]
  R2 = Resistor [tolerance=±5% resistance=1k package=THT]
  LED3 = smd LED [color="Green (565nm)" package="1206 [SMD]"]
  R3 = Resistor [tolerance=±5% resistance=1k package=THT]
  LED4 = smd LED [color="Green (565nm)" package="1206 [SMD]"]
  R4 = Resistor [tolerance=±5% resistance=1k package=THT]
  J1 = Camdenboss CTB0158-2 [part_number=CTB0158-2 package=THT]
  J2 = Camdenboss CTB0158-2 [part_number=CTB0158-2 package=THT]
  J3 = Camdenboss CTB0158-2 [part_number=CTB0158-2 package=THT]
  J4 = Camdenboss CTB0158-2 [part_number=CTB0158-2 package=THT]
  R5 = Resistor [tolerance=±5% resistance=1k package=THT]
  R6 = Resistor [tolerance=±5% resistance=1k package=THT]
  R7 = Resistor [tolerance=±5% resistance=1k package=THT]  # not connected
  R8 = Resistor [tolerance=±5% resistance=1k package=THT]  # not connected
  Part1 = Arduino Uno (Rev3)
  Part2 = Real Time Clock Module - DS1307 RTC Breakout Board
  C1 = Electrolytic Capacitor [capacitance=1μF package="0405 [SMD, electrolytic]"]
  J5 = Camdenboss CTB0158-2 [part_number=CTB0158-2 package=THT]
  C2 = Electrolytic Capacitor [capacitance=1μF package="0405 [SMD, electrolytic]"]
  J6 = Camdenboss CTB0158-2 [part_number=CTB0158-2 package=THT]
  C3 = Electrolytic Capacitor [capacitance=1μF package="0405 [SMD, electrolytic]"]
  C4 = Electrolytic Capacitor [capacitance=1μF package="0405 [SMD, electrolytic]"]
  J7 = Camdenboss CTB0158-2 [part_number=CTB0158-2 package=THT]
  J8 = Camdenboss CTB0158-2 [part_number=CTB0158-2 package=THT]
  R9 = Resistor [tolerance=±5% resistance=1k package=THT]
  C5 = Electrolytic Capacitor [capacitance=1μF package="0405 [SMD, electrolytic]"]
  J9 = Camdenboss CTB0158-2 [part_number=CTB0158-2 package=THT]
  R10 = Resistor [tolerance=±5% resistance=1k package=THT]
  C6 = Electrolytic Capacitor [capacitance=1μF package="0405 [SMD, electrolytic]"]
  J10 = Camdenboss CTB0158-2 [part_number=CTB0158-2 package=THT]
  DS1 = DS18B20 1-Wire Temperature Sensor [part_number=DS18B20]
  R11 = Resistor [tolerance=±10% resistance=4.7k package=THT]

nets:
  N1: U1.Pin_1, LED1.cathode
  GND: U1.Pin_2, U1.Pin_3, U2.Pin_2, U2.Pin_3, U3.Pin_2, U3.Pin_3, U4.Pin_2, U4.Pin_3, J1.pin1, J2.pin1, J3.pin1, J4.pin1, Part2.GND, C1.-, J5.pin2, C2.-, J6.pin2, C3.-, C4.-, J7.pin2, J8.pin2, C5.-, J9.pin2, C6.-, J10.pin2, DS1.GND
  N2: U1.Pin_4, R5.Pin_0, Part1.D3_PWM
  N3: U2.Pin_1, LED2.cathode
  N4: U2.Pin_4, R6.Pin_0, Part1.D4
  N5: U3.Pin_1, LED3.cathode
  N6: U3.Pin_4, Part1.D7
  N7: U4.Pin_1, LED4.cathode
  N8: U4.Pin_4, Part1.D8
  N9: LED1.anode, R1.Pin_1
  N10: R1.Pin_0, J1.pin2
  N11: LED2.anode, R2.Pin_1
  N12: R2.Pin_0, J2.pin2
  N13: LED3.anode, R3.Pin_1
  N14: R3.Pin_0, J3.pin2
  N15: LED4.anode, R4.Pin_1
  N16: R4.Pin_0, J4.pin2
  N17: Part1.A0, C1.+, J5.pin1
  N18: Part1.A1, C2.+, J6.pin1
  N19: Part1.A2, C3.+, J7.pin1
  N20: Part1.A3, C4.+, J8.pin1
  N21: Part1.D9_PWM, DS1.DQ, R11.Pin_1
  N22: Part1.A4/SDA, Part2.SDA
  N23: Part1.A5/SCL, Part2.SCL
  N24: Part1.D5_PWM, R10.Pin_1, C6.+
  N25: Part1.D6_PWM, R9.Pin_1, C5.+
  5V: Part2.5V, DS1.VDD, R11.Pin_0
  N26: R9.Pin_0, J9.pin1
  N27: R10.Pin_0, J10.pin1
