# Fritzing sketch PLC3 (saved by Fritzing 0.9.3b)
breadboards: 2

parts:
  U1 = Module 4 Relais 5V [package="Module 4 Relais 5V"]  # not connected
  OLED_I2C1 = OLED 128x64 I2C Monochrome Display  # not connected
  Part1 = Real Time Clock Module - DS1307 RTC Breakout Board  # not connected
  Part2 = Arduino Uno (Rev3)  # not connected
  Part3 = Bluetooth HC-05 Macho  # not connected
  DS1 = DS18B20 1-Wire Temperature Sensor [part_number=DS18B20]
  U2 = Sharp PC817 [package=THT]
  U3 = Sharp PC817 [package=THT]
  U4 = Sharp PC817 [package=THT]
  U5 = Sharp PC817 [package=THT]
  LED1 = smd LED [color="Red (633nm)" package="0805 [SMD]"]
  LED2 = smd LED [color="Red (633nm)" package="0805 [SMD]"]
  LED3 = smd LED [color="Red (633nm)" package="0805 [SMD]"]
  LED4 = smd LED [color="Red (633nm)" package="0805 [SMD]"]
  R1 = Resistor [tolerance=±5% resistance=1k package="2010 [SMD]"]
  R2 = Resistor [tolerance=±5% resistance=1k package="2010 [SMD]"]
  R3 = Resistor [tolerance=±5% resistance=1k package="2010 [SMD]"]
  R4 = Resistor [tolerance=±5% resistance=1k package="2010 [SMD]"]
  R5 = Resistor [tolerance=±5% resistance=1k package="2010 [SMD]"]
  R6 = Resistor [tolerance=±5% resistance=1k package="2010 [SMD]"]
  R7 = Resistor [tolerance=±5% resistance=1k package="2010 [SMD]"]
  R8 = Resistor [tolerance=±5% resistance=1k package="2010 [SMD]"]
  R9 = Resistor [tolerance=±5% resistance=1k package="2010 [SMD]"]
  C3 = Electrolytic Capacitor [capacitance=1μF package="0405 [SMD, electrolytic]"]
  C4 = Electrolytic Capacitor [capacitance=1μF package="0405 [SMD, electrolytic]"]
  R10 = Resistor [tolerance=±5% resistance=1k package="2010 [SMD]"]
  R11 = Resistor [tolerance=±5% resistance=1k package="2010 [SMD]"]
  C5 = Electrolytic Capacitor [capacitance=1μF package="0405 [SMD, electrolytic]"]
  C6 = Electrolytic Capacitor [capacitance=1μF package="0405 [SMD, electrolytic]"]
  C7 = Electrolytic Capacitor [capacitance=1μF package="0405 [SMD, electrolytic]"]
  C8 = Electrolytic Capacitor [capacitance=1μF package="0405 [SMD, electrolytic]"]

nets:
  N1: DS1.GND, U2.Pin_3, U3.Pin_3, U4.Pin_3, U5.Pin_3
  N2: DS1.DQ, R11.Pin_1
  N3: DS1.VDD, R5.Pin_0, R6.Pin_0, R7.Pin_0, R8.Pin_0
  N4: U2.Pin_2, U3.Pin_2, U4.Pin_2, U5.Pin_2
  N5: U2.Pin_4, R5.Pin_1
  N6: U3.Pin_4, R6.Pin_1
  N7: U4.Pin_4, R7.Pin_1
  N8: U5.Pin_4, R8.Pin_1
  N9: LED1.anode, R4.Pin_1
  N10: LED2.anode, R3.Pin_1
  N11: LED3.anode, R2.Pin_1
  N12: LED4.anode, R1.Pin_1
  N13: R9.Pin_1, C3.+
  N14: C3.-, C4.-, C5.-, C6.-, C7.-, C8.-
  N15: C4.+, R10.Pin_1

notes:
  Analog Outputs
  Digital Inputs
  Analog Inputs

custom parts:
  Module 4 Relais 5V: Module 4 Relais 5V 4x SPD-06VDC-SD-C
