# Fritzing sketch bluetooth (saved by Fritzing 0.9.3b)
breadboards: 1

parts:
  Part1 = Bluetooth HC-05 Macho  # not connected
  Part2 = Arduino Uno (Rev3)
  R1 = Resistor [tolerance=±5% resistance=2.2k package="0805 [SMD]"]
  R2 = Resistor [tolerance=±5% resistance=1k package="0805 [SMD]"]

nets:
  N1: Part2.D1/TX, R2.Pin_1
  N2: Part2.GND, R1.Pin_0
  N3: R1.Pin_1, R2.Pin_0
